# Fritzing sketch schema_panneau (saved by Fritzing 0.8.0b)
breadboards: 1

parts:
  LED1 = RGB LED (com. anode, rbg) [package="5 mm [THT]"]
  R1 = Resistor [tolerance=±5% resistance=15 package=THT]
  R3 = Resistor [tolerance=±5% resistance=47 package=THT]
  R4 = Resistor [tolerance=±5% resistance=47 package=THT]
  R5 = Resistor [tolerance=±5% resistance=10 package=THT]
  R6 = Resistor [tolerance=±5% resistance=220 package=THT]
  R7 = Resistor [tolerance=±5% resistance=220 package=THT]
  LED2 = LED - 5mm [color="White (8000K)" package="5 mm [THT]"]
  R8 = Resistor [tolerance=±5% resistance=220 package=THT]
  J1 = Peltier Element  # not connected
  J2 = Peltier Element  # not connected
  S1 = Pushbutton [package="[THT]"]
  R9 = Resistor [tolerance=±5% resistance=220 package=THT]  # not connected
  R10 = Resistor [tolerance=±5% resistance=220 package=THT]
  R11 = Resistor [tolerance=±5% resistance=220 package=THT]
  R12 = Resistor [tolerance=±5% resistance=220 package=THT]
  R13 = Resistor [tolerance=±5% resistance=220 package=THT]
  R14 = Resistor [tolerance=±5% resistance=220 package=THT]
  R15 = Resistor [tolerance=±5% resistance=220 package=THT]
  R16 = Resistor [tolerance=±5% resistance=220 package=THT]
  R17 = Resistor [tolerance=±5% resistance=220 package=THT]
  S2 = Pushbutton [package="[THT]"]
  S3 = Pushbutton [package="[THT]"]
  S4 = Pushbutton [package="[THT]"]
  R18 = Resistor [tolerance=±5% resistance=220 package=THT]
  R19 = Resistor [tolerance=±5% resistance=220 package=THT]
  S5 = Pushbutton [package="[THT]"]
  Composants1 = IBoard - Multi-type communication board Platform Based On Arduino

nets:
  N1: LED1.red_cathode, R5.Pin_1
  N2: LED1.common_anode, S1.Pin_3, S1.Pin_4, S2.Pin_3, S2.Pin_4, S3.Pin_3, S3.Pin_4, S4.Pin_3, S4.Pin_4, S5.Pin_3, S5.Pin_4, Composants1.D1(TX), Composants1.GND
  N3: LED1.blue_cathode, R3.Pin_1
  N4: LED1.green_cathode, R4.Pin_1
  N5: R1.Pin_0, Composants1.A3
  N6: R6.Pin_0, Composants1.A2
  N7: R7.Pin_0, Composants1.A1
  N8: LED2.cathode, Composants1.+3V3
  N9: LED2.anode, R8.Pin_1
  N10: R8.Pin_0, Composants1.A4
  N11: S1.Pin_1, S1.Pin_2, R13.Pin_0, R14.Pin_0, R16.Pin_0, R17.Pin_0, R18.Pin_1, R19.Pin_1
  N12: R10.Pin_0, R11.Pin_0, R12.Pin_1, R15.Pin_1, S3.Pin_1, S3.Pin_2
  N13: R10.Pin_1, R11.Pin_1, S4.Pin_1, S4.Pin_2
  N14: R12.Pin_0, R13.Pin_1, R14.Pin_1, R15.Pin_0, R16.Pin_1, R17.Pin_1, S2.Pin_1, S2.Pin_2
  N15: R18.Pin_0, R19.Pin_0, S5.Pin_1, S5.Pin_2

custom parts:
  IBoard - Multi-type communication board Platform Based On Arduino: Multi-type communication board Platform Based On Arduino by Iteadstudio Principal features : Electronic Brick Ports XBee socket Support micro SD card WIZnet ethernet port with POE nRF24L01+ module interface FOCA socket The official support forum: support@iteadstudio.com
